// Logisim project 4-bit processor.circ as structural Verilog: 18 circuits, main circuit main
module main (
  input  [3:0] INPR,
  output E
);

  wire and_1_out, clock_1_out, main_cont_1_dr_ld, main_cont_1_e__clr, main_cont_1_hlt, main_cont_1_outr_ld;
  wire [1:0] main_cont_1_ir_ld_bus, main_cont_1_m_ld_bus;
  wire [2:0] main_cont_1_ar_inc_ld_bus, main_cont_1_pc_inc_ld_bus;
  wire [3:0] AC_output, alu_4_1_output, AR_output, DR_output, IR_output1, IR_output2,
       main_cont_1_ac_inc_ld_clr_bus, OUTR_output, PC_output;
  wire [6:0] main_cont_1_alu;
  wire [7:0] controlled_buffer_1_out, ram_1_data;

  Clock clock_1 (.out(clock_1_out));
  and and_1 (and_1_out, ~main_cont_1_hlt, clock_1_out);  // AND_Gate
  Main_Cont main_cont_1 (
    .IR4__7(IR_output2), .CLK(and_1_out), .HLT(main_cont_1_hlt), .E__CLR(main_cont_1_e__clr),
    .M_LD_BUS(main_cont_1_m_ld_bus), .AR_INC_LD_BUS(main_cont_1_ar_inc_ld_bus),
    .PC_INC_LD_BUS(main_cont_1_pc_inc_ld_bus), .DR_LD(main_cont_1_dr_ld), .IR_LD_BUS(main_cont_1_ir_ld_bus),
    .OUTR_LD(main_cont_1_outr_ld), .AC_INC_LD_CLR_BUS(main_cont_1_ac_inc_ld_clr_bus), .ALU(main_cont_1_alu));
  ALU_4 alu_4_1 (
    .AC(AC_output), .DR(DR_output), .INPR(INPR), .AND(main_cont_1_alu[0]), .ADD(main_cont_1_alu[1]),
    .ld_DR(main_cont_1_alu[2]), .CMA(main_cont_1_alu[3]), .CIR(main_cont_1_alu[4]), .CIL(main_cont_1_alu[5]),
    .ld_INPR(main_cont_1_alu[6]), .output_E(E), .CLK(and_1_out), .CLR(main_cont_1_e__clr),
    .OUTPUT(alu_4_1_output));
  _4_REG AR (
    .INPUT(controlled_buffer_1_out[3:0]), .CLK(and_1_out), .INC(main_cont_1_ar_inc_ld_bus[2]),
    .LD(main_cont_1_ar_inc_ld_bus[1]), .OUTPUT(AR_output));  // open: CLR
  _4_REG PC (
    .INPUT(controlled_buffer_1_out[3:0]), .CLK(and_1_out), .INC(main_cont_1_pc_inc_ld_bus[2]),
    .LD(main_cont_1_pc_inc_ld_bus[1]), .OUTPUT(PC_output));  // open: CLR
  _4_REG DR (
    .INPUT(controlled_buffer_1_out[3:0]), .CLK(and_1_out), .LD(main_cont_1_dr_ld), .OUTPUT(DR_output));  // open: INC, CLR
  _4_REG AC (
    .INPUT(alu_4_1_output), .CLK(and_1_out), .INC(main_cont_1_ac_inc_ld_clr_bus[3]),
    .LD(main_cont_1_ac_inc_ld_clr_bus[2]), .CLR(main_cont_1_ac_inc_ld_clr_bus[1]), .OUTPUT(AC_output));
  // Probe on IR_output2
  _8_REG IR (
    .INPUT(controlled_buffer_1_out), .CLK(and_1_out), .LD(main_cont_1_ir_ld_bus[1]), .OUTPUT1(IR_output1),
    .OUTPUT2(IR_output2));
  // Probe on OUTR_output
  _4_REG OUTR (
    .INPUT(controlled_buffer_1_out[3:0]), .CLK(and_1_out), .LD(main_cont_1_outr_ld), .OUTPUT(OUTR_output));  // open: INC, CLR
  RAM #(.addrWidth(4), .bus("separate")) ram_1 (
    .addr(AR_output), .din(controlled_buffer_1_out), .data(ram_1_data), .str(main_cont_1_m_ld_bus[1]),
    .clk(and_1_out));  // open: sel, ld, clr
  // Probe on AR_output
  // Probe on PC_output
  // Probe on main_cont_1_pc_inc_ld_bus[0]
  // Probe on DR_output
  // Probe on AC_output
  // Probe on IR_output1
  assign controlled_buffer_1_out = main_cont_1_ir_ld_bus[0] ? {4'b0000, IR_output1} : 8'bz;  // Controlled_Buffer controlled_buffer_1
  assign controlled_buffer_1_out = main_cont_1_m_ld_bus[0] ? ram_1_data : 8'bz;  // Controlled_Buffer controlled_buffer_2
  assign controlled_buffer_1_out = main_cont_1_ar_inc_ld_bus[0] ? {4'b0000, AR_output} : 8'bz;  // Controlled_Buffer controlled_buffer_3
  assign controlled_buffer_1_out = main_cont_1_pc_inc_ld_bus[0] ? {4'b0000, PC_output} : 8'bz;  // Controlled_Buffer controlled_buffer_4
  assign controlled_buffer_1_out = main_cont_1_ac_inc_ld_clr_bus[0] ? {4'b0000, AC_output} : 8'bz;  // Controlled_Buffer controlled_buffer_5
endmodule

module _4_REG (
  input  INC,
  input  LD,
  input  [3:0] INPUT,
  input  CLR,
  input  CLK,
  output [3:0] OUTPUT
);

  wire and_1_out, and_2_out, and_3_out, and_4_out, and_5_out, and_6_out, and_7_out, and_8_out, and_9_out,
       and_10_out, and_11_out, and_12_out, not_1_out, not_2_out, not_3_out, not_4_out, not_5_out, not_6_out,
       or_1_out, or_2_out, or_3_out, or_4_out, or_5_out, or_6_out, or_7_out, or_8_out;

  not not_1 (not_1_out, LD);
  not not_2 (not_2_out, INPUT[0]);
  not not_3 (not_3_out, INPUT[1]);
  not not_4 (not_4_out, INPUT[2]);
  not not_5 (not_5_out, INPUT[3]);
  and and_1 (and_1_out, INC, not_1_out);
  not not_6 (not_6_out, not_1_out);
  and and_2 (and_2_out, not_6_out, INPUT[0]);
  and and_3 (and_3_out, not_6_out, not_2_out);
  and and_4 (and_4_out, not_6_out, INPUT[1]);
  and and_5 (and_5_out, not_6_out, not_3_out);
  and and_6 (and_6_out, not_6_out, INPUT[2]);
  and and_7 (and_7_out, not_6_out, not_4_out);
  and and_8 (and_8_out, not_6_out, INPUT[3]);
  and and_9 (and_9_out, not_6_out, not_5_out);
  and and_10 (and_10_out, and_1_out, OUTPUT[0]);
  and and_11 (and_11_out, and_1_out, OUTPUT[0], OUTPUT[1]);
  and and_12 (and_12_out, and_1_out, OUTPUT[0], OUTPUT[1], OUTPUT[2]);
  or or_1 (or_1_out, and_2_out, and_1_out);
  or or_2 (or_2_out, and_3_out, and_1_out);
  or or_3 (or_3_out, and_4_out, and_10_out);
  or or_4 (or_4_out, and_10_out, and_5_out);
  or or_5 (or_5_out, and_6_out, and_11_out);
  or or_6 (or_6_out, and_11_out, and_7_out);
  or or_7 (or_7_out, and_8_out, and_12_out);
  or or_8 (or_8_out, and_12_out, and_9_out);
  J_K_Flip_Flop j_k_ff_1 (.J(or_1_out), .clk(CLK), .K(or_2_out), .Q(OUTPUT[0]), .reset(CLR));  // open: Qn, preset, en
  J_K_Flip_Flop j_k_ff_2 (.J(or_3_out), .clk(CLK), .K(or_4_out), .Q(OUTPUT[1]), .reset(CLR));  // open: Qn, preset, en
  J_K_Flip_Flop j_k_ff_3 (.J(or_5_out), .clk(CLK), .K(or_6_out), .Q(OUTPUT[2]), .reset(CLR));  // open: Qn, preset, en
  J_K_Flip_Flop j_k_ff_4 (.J(or_7_out), .clk(CLK), .K(or_8_out), .Q(OUTPUT[3]), .reset(CLR));  // open: Qn, preset, en
endmodule

module _8_REG (
  input  [7:0] INPUT,
  input  CLK,
  input  LD,
  output [3:0] OUTPUT1,
  output [3:0] OUTPUT2
);

  _4_REG u_4_reg_1 (.INPUT(INPUT[3:0]), .CLK(CLK), .LD(LD), .OUTPUT(OUTPUT1));  // open: INC, CLR
  _4_REG u_4_reg_2 (.INPUT(INPUT[7:4]), .CLK(CLK), .LD(LD), .OUTPUT(OUTPUT2));  // open: INC, CLR
endmodule

module ALU_1 (
  input  INPR,
  input  DR,
  input  AC,
  input  Cin,
  input  AND,
  input  ADD,
  input  ld_DR,
  input  CMA,
  input  CIR,
  input  CIL,
  input  ld_INPR,
  input  i_1,
  input  i_1_2,
  output OUTPUT,
  output Cout
);

  wire adder_1_out, and_1_out, and_2_out, and_3_out, and_4_out, and_5_out, and_6_out, and_7_out, and_8_out,
       not_1_out;

  Adder #(.width(1)) adder_1 (.a(AC), .b(DR), .out(adder_1_out), .cin(Cin), .cout(Cout));
  and and_1 (and_1_out, AND, and_2_out);
  and and_2 (and_2_out, AC, DR);
  and and_3 (and_3_out, ADD, adder_1_out);
  and and_4 (and_4_out, ld_DR, DR);
  and and_5 (and_5_out, CMA, not_1_out);
  not not_1 (not_1_out, AC);
  and and_6 (and_6_out, CIR, i_1_2);
  and and_7 (and_7_out, CIL, i_1);
  and and_8 (and_8_out, ld_INPR, INPR);
  or or_1 (OUTPUT, and_1_out, and_3_out, and_4_out, and_5_out, and_6_out, and_7_out, and_8_out);
endmodule

module ALU_4 (
  input  [3:0] AC,
  input  [3:0] DR,
  input  [3:0] INPR,
  input  AND,
  input  ADD,
  input  ld_DR,
  input  CMA,
  input  CIR,
  input  CIL,
  input  ld_INPR,
  input  CLK,
  input  CLR,
  output [3:0] OUTPUT,
  output output_E
);

  wire alu_1_1_cout, alu_1_2_cout, alu_1_3_cout, alu_1_4_cout, e_1_ac_0__ac_i_1, e_1_ac_0__cin,
       e_1_ac_3__ac_i_1;

  ALU_1 alu_1_1 (
    .AND(AND), .ADD(ADD), .ld_DR(ld_DR), .CMA(CMA), .CIR(CIR), .CIL(CIL), .ld_INPR(ld_INPR),
    .i_1(e_1_ac_0__ac_i_1), .i_1_2(AC[1]), .INPR(INPR[0]), .DR(DR[0]), .AC(AC[0]), .Cin(e_1_ac_0__cin),
    .Cout(alu_1_1_cout), .OUTPUT(OUTPUT[0]));
  ALU_1 alu_1_2 (
    .AND(AND), .ADD(ADD), .ld_DR(ld_DR), .CMA(CMA), .CIR(CIR), .CIL(CIL), .ld_INPR(ld_INPR), .i_1(AC[0]),
    .i_1_2(AC[2]), .INPR(INPR[1]), .DR(DR[1]), .AC(AC[1]), .Cin(alu_1_1_cout), .Cout(alu_1_2_cout),
    .OUTPUT(OUTPUT[1]));
  ALU_1 alu_1_3 (
    .AND(AND), .ADD(ADD), .ld_DR(ld_DR), .CMA(CMA), .CIR(CIR), .CIL(CIL), .ld_INPR(ld_INPR), .i_1(AC[1]),
    .i_1_2(AC[3]), .INPR(INPR[2]), .DR(DR[2]), .AC(AC[2]), .Cin(alu_1_2_cout), .Cout(alu_1_3_cout),
    .OUTPUT(OUTPUT[2]));
  ALU_1 alu_1_4 (
    .AND(AND), .ADD(ADD), .ld_DR(ld_DR), .CMA(CMA), .CIR(CIR), .CIL(CIL), .ld_INPR(ld_INPR), .i_1(AC[2]),
    .i_1_2(e_1_ac_3__ac_i_1), .INPR(INPR[3]), .DR(DR[3]), .AC(AC[3]), .Cin(alu_1_3_cout),
    .Cout(alu_1_4_cout), .OUTPUT(OUTPUT[3]));
  E e_1 (
    .AC_3__Cout(alu_1_4_cout), .AC_3__output(AC[3]), .AC_0__output(AC[0]), .CIL(CIL), .CIR(CIR), .ADD(ADD),
    .CLK(CLK), .CLR(CLR), .output_E(output_E), .AC_0__ac_i_1(e_1_ac_0__ac_i_1),
    .AC_3__ac_i_1(e_1_ac_3__ac_i_1), .AC_0__cin(e_1_ac_0__cin));
endmodule

// PC_Cont
module Cont_PC (
  input  D4,
  input  D5,
  input  D6,
  input  T0,
  input  T1,
  input  T3,
  input  T4,
  output PC_INC,
  output PC_LD,
  output PC_BUS
);

  wire and_1_out, and_2_out, and_3_out, or_1_out;

  or or_1 (or_1_out, D6, D4);
  and and_1 (and_1_out, or_1_out, T3);
  and and_2 (and_2_out, D5, T4);
  or or_2 (PC_LD, and_1_out, and_2_out);
  or or_3 (PC_BUS, T0, and_3_out);
  and and_3 (and_3_out, T3, D5);

  assign PC_INC = T1;
endmodule

// Main_Con
module Main_Cont (
  input  [3:0] IR4__7,
  input  CLK,
  output [1:0] M_LD_BUS,
  output [2:0] AR_INC_LD_BUS,
  output [2:0] PC_INC_LD_BUS,
  output DR_LD,
  output [1:0] IR_LD_BUS,
  output OUTR_LD,
  output [3:0] AC_INC_LD_CLR_BUS,
  output [6:0] ALU,
  output HLT,
  output E__CLR
);

  wire decoder_1_out15, decoder_2_out0, decoder_2_out1, decoder_2_out2, sc_clr_1_sc_clr;
  wire [1:0] decoder_2_out4;
  wire [3:0] Counter_output;
  wire [14:0] decoder_1_out0;

  SC_CLR sc_clr_1 (
    .T3(decoder_2_out4[1]), .T4(decoder_2_out4[0]), .D0(decoder_1_out0[0]), .D1(decoder_1_out0[1]),
    .D2(decoder_1_out0[2]), .D3(decoder_1_out0[3]), .D4(decoder_1_out0[4]), .D5(decoder_1_out0[5]),
    .D6(decoder_1_out0[6]), .D7(decoder_1_out0[7]), .D8(decoder_1_out0[8]), .D9(decoder_1_out0[9]),
    .D10(decoder_1_out0[10]), .D11(decoder_1_out0[11]), .D12(decoder_1_out0[12]), .D13(decoder_1_out0[13]),
    .D14(decoder_1_out0[14]), .SC_CLR(sc_clr_1_sc_clr));
  // Probe on IR4__7
  Decoder #(.select(4)) decoder_1 (
    .out0(decoder_1_out0[0]), .out1(decoder_1_out0[1]), .out2(decoder_1_out0[2]), .out3(decoder_1_out0[3]),
    .out4(decoder_1_out0[4]), .out5(decoder_1_out0[5]), .out6(decoder_1_out0[6]), .out7(decoder_1_out0[7]),
    .out8(decoder_1_out0[8]), .out9(decoder_1_out0[9]), .out10(decoder_1_out0[10]),
    .out11(decoder_1_out0[11]), .out12(decoder_1_out0[12]), .out13(decoder_1_out0[13]),
    .out14(decoder_1_out0[14]), .out15(decoder_1_out15), .sel(IR4__7));  // open: en
  Decoder #(.select(4)) decoder_2 (
    .out0(decoder_2_out0), .out1(decoder_2_out1), .out2(decoder_2_out2), .out3(decoder_2_out4[1]),
    .out4(decoder_2_out4[0]), .sel(Counter_output));  // open: out5, out6, out7, out8, out9, out10, out11, out12, out13, out14, out15, en
  Counter Counter (.CLK(CLK), .SC_CLR(sc_clr_1_sc_clr), .OUTPUT(Counter_output));
  and and_1 (HLT, decoder_1_out15, decoder_2_out4[1]);
  and and_2 (E__CLR, decoder_1_out0[8], decoder_2_out4[1]);
  REGS_Con regs_con_1 (
    .T0(decoder_2_out0), .T1(decoder_2_out1), .T2(decoder_2_out2), .T3(decoder_2_out4[1]),
    .T4(decoder_2_out4[0]), .D0(decoder_1_out0[0]), .D1(decoder_1_out0[1]), .D2(decoder_1_out0[2]),
    .D3(decoder_1_out0[3]), .D4(decoder_1_out0[4]), .D5(decoder_1_out0[5]), .D6(decoder_1_out0[6]),
    .D7(decoder_1_out0[7]), .D8(decoder_1_out0[8]), .D9(decoder_1_out0[9]), .D10(decoder_1_out0[10]),
    .D11(decoder_1_out0[11]), .D12(decoder_1_out0[12]), .D13(decoder_1_out0[13]), .D14(decoder_1_out0[14]),
    .PC_INC_LD_BUS(PC_INC_LD_BUS), .M_LD_BUS(M_LD_BUS), .AR_INC_LD_BUS(AR_INC_LD_BUS), .DR_LD(DR_LD),
    .IR_LD_BUS(IR_LD_BUS), .OUTR_LD(OUTR_LD), .AC_INC_LD_CLR_BUS(AC_INC_LD_CLR_BUS), .ALU(ALU));

  // Notes on the sheet:
  //   D0..15
  //   T0..4
endmodule

// M_Cont
module Cont_M (
  input  T1,
  input  T3,
  input  D0,
  input  D1,
  input  D2,
  input  D3,
  input  D5,
  input  D6,
  output M_LD,
  output M_BUS
);

  wire and_2_out, or_1_out, or_2_out;

  or or_1 (or_1_out, D3, D5);
  and and_1 (M_LD, or_1_out, T3);
  or or_2 (or_2_out, D6, D2, D1, D0);
  and and_2 (and_2_out, or_2_out, T3);
  or or_3 (M_BUS, and_2_out, T1);
endmodule

// AR_Cont
module Cont_AR (
  input  D4,
  input  D5,
  input  T0,
  input  T2,
  input  T3,
  input  T4,
  output AR_INC,
  output AR_LD,
  output AR_BUS
);

  wire and_2_out, and_3_out;

  and and_1 (AR_INC, T3, D5);
  or or_1 (AR_LD, T2, T0);
  and and_2 (and_2_out, T3, D4);
  or or_2 (AR_BUS, and_2_out, and_3_out);
  and and_3 (and_3_out, T4, D5);
endmodule

// DR_Cont
module Cont_DR (
  input  T3,
  input  D0,
  input  D1,
  input  D2,
  output DR_LD
);

  wire or_1_out;

  or or_1 (or_1_out, D2, D1, D0);
  and and_1 (DR_LD, or_1_out, T3);
endmodule

// IR_C
module Cont_IR (
  input  T2,
  input  T1,
  output IR_LD,
  output IR_BUS
);


  assign IR_BUS = T2;
  assign IR_LD = T1;
endmodule

// OUTR
module Cont_OUTR (
  input  D14,
  input  T3,
  output OUTR_LD
);

  and and_1 (OUTR_LD, T3, D14);
endmodule

// AC_Cont
module Cont_AC (
  input  T3,
  input  T4,
  input  D0,
  input  D1,
  input  D2,
  input  D3,
  input  D7,
  input  D9,
  input  D10,
  input  D11,
  input  D12,
  input  D13,
  input  D14,
  output AC_INC,
  output AC_LD,
  output AC_CLR,
  output AC_BUS
);

  wire and_2_out, and_3_out, or_1_out, or_2_out, or_4_out;

  or or_1 (or_1_out, D13, D12, D11, D9);
  or or_2 (or_2_out, D2, D1, D0);
  and and_1 (AC_INC, D10, T3);
  and and_2 (and_2_out, or_1_out, T3);
  or or_3 (AC_LD, and_2_out, and_3_out);
  and and_3 (and_3_out, T4, or_2_out);
  and and_4 (AC_CLR, D7, T3);
  or or_4 (or_4_out, D14, D3);
  and and_5 (AC_BUS, or_4_out, T3);
endmodule

// ALU_Cont
module Cont_ALU (
  input  T3,
  input  T4,
  input  D0,
  input  D1,
  input  D2,
  input  D9,
  input  D11,
  input  D12,
  input  D13,
  output [6:0] OUTPUT
);

  and and_1 (OUTPUT[0], D0, T4);
  and and_2 (OUTPUT[1], D1, T4);
  and and_3 (OUTPUT[2], D2, T4);
  and and_4 (OUTPUT[3], D9, T3);
  and and_5 (OUTPUT[4], D11, T3);
  and and_6 (OUTPUT[5], D12, T3);
  and and_7 (OUTPUT[6], D13, T3);
endmodule

module SC_CLR (
  input  T3,
  input  T4,
  input  D0,
  input  D1,
  input  D2,
  input  D3,
  input  D4,
  input  D5,
  input  D6,
  input  D7,
  input  D8,
  input  D9,
  input  D10,
  input  D11,
  input  D12,
  input  D13,
  input  D14,
  output SC_CLR
);

  wire and_1_out, and_2_out, or_1_out, or_2_out;

  or or_1 (or_1_out, D14, D13, D12, D11, D10, D9, D8, D7, D6, D4, D3);
  or or_2 (or_2_out, D5, D2, D1, D0);
  and and_1 (and_1_out, or_1_out, T3);
  or or_3 (SC_CLR, and_1_out, and_2_out);
  and and_2 (and_2_out, or_2_out, T4);
endmodule

module Counter (
  input  CLK,
  input  SC_CLR,
  output [3:0] OUTPUT
);

  wire and_1_out, register_1_q;

  Register #(.width(1)) register_1 (.D(SC_CLR), .Q(register_1_q), .clk(CLK), .clr(and_1_out));  // open: en
  and and_1 (and_1_out, CLK, SC_CLR);
  Counter_part #(.width(4), .max('hf)) counter_1 (
    .count(1'b1), .Q(OUTPUT), .clk(CLK), .clr(register_1_q));  // open: load, D, carry
endmodule

module REGS_Con (
  input  T0,
  input  T1,
  input  T2,
  input  T3,
  input  T4,
  input  D0,
  input  D1,
  input  D2,
  input  D3,
  input  D4,
  input  D5,
  input  D6,
  input  D7,
  input  D8,
  input  D9,
  input  D10,
  input  D11,
  input  D12,
  input  D13,
  input  D14,
  output [2:0] PC_INC_LD_BUS,
  output [1:0] M_LD_BUS,
  output [2:0] AR_INC_LD_BUS,
  output DR_LD,
  output [1:0] IR_LD_BUS,
  output OUTR_LD,
  output [3:0] AC_INC_LD_CLR_BUS,
  output [6:0] ALU
);

  Cont_PC cont_pc_1 (
    .D4(D4), .D5(D5), .D6(D6), .T0(T0), .T1(T1), .T3(T3), .T4(T4), .PC_INC(PC_INC_LD_BUS[2]),
    .PC_LD(PC_INC_LD_BUS[1]), .PC_BUS(PC_INC_LD_BUS[0]));
  Cont_M cont_m_1 (
    .T1(T1), .T3(T3), .D0(D0), .D1(D1), .D2(D2), .D3(D3), .D5(D5), .D6(D6), .M_LD(M_LD_BUS[1]),
    .M_BUS(M_LD_BUS[0]));
  Cont_AR cont_ar_1 (
    .D4(D4), .D5(D5), .T0(T0), .T2(T2), .T3(T3), .T4(T4), .AR_INC(AR_INC_LD_BUS[2]),
    .AR_LD(AR_INC_LD_BUS[1]), .AR_BUS(AR_INC_LD_BUS[0]));
  Cont_DR cont_dr_1 (.T3(T3), .D0(D0), .D1(D1), .D2(D2), .DR_LD(DR_LD));
  Cont_IR cont_ir_1 (.T2(T2), .T1(T1), .IR_LD(IR_LD_BUS[1]), .IR_BUS(IR_LD_BUS[0]));
  Cont_OUTR cont_outr_1 (.D14(D14), .T3(T3), .OUTR_LD(OUTR_LD));
  Cont_AC cont_ac_1 (
    .T3(T3), .T4(T4), .D0(D0), .D1(D1), .D2(D2), .D3(D3), .D7(D7), .D9(D9), .D10(D10), .D11(D11), .D12(D12),
    .D13(D13), .D14(D14), .AC_INC(AC_INC_LD_CLR_BUS[3]), .AC_LD(AC_INC_LD_CLR_BUS[2]),
    .AC_CLR(AC_INC_LD_CLR_BUS[1]), .AC_BUS(AC_INC_LD_CLR_BUS[0]));
  Cont_ALU cont_alu_1 (
    .T3(T3), .T4(T4), .D0(D0), .D1(D1), .D2(D2), .D9(D9), .D11(D11), .D12(D12), .D13(D13), .OUTPUT(ALU));
endmodule

module E (
  input  AC_3__Cout,
  input  AC_3__output,
  input  AC_0__output,
  input  CIL,
  input  CIR,
  input  ADD,
  input  CLK,
  input  CLR,
  output output_E,
  output AC_0__ac_i_1,
  output AC_3__ac_i_1,
  output AC_0__cin
);

  wire and_1_out, and_2_out, and_3_out, and_4_out, and_5_out, d_ff_1_q, not_1_out, or_1_out, or_2_out;

  or or_1 (or_1_out, AC_3__Cout, AC_3__output, AC_0__output);
  and and_1 (and_1_out, AC_3__Cout, ADD);
  and and_2 (and_2_out, AC_0__output, CIR);
  and and_3 (and_3_out, AC_3__output, CIL);
  or or_2 (or_2_out, and_1_out, and_2_out, and_3_out);
  and and_4 (and_4_out, or_2_out, or_1_out);
  and and_5 (and_5_out, or_1_out, not_1_out);
  not not_1 (not_1_out, or_2_out);
  D_Flip_Flop d_ff_1 (.clk(CLK), .D(output_E), .Q(d_ff_1_q), .reset(CLR));  // open: Qn, preset, en
  J_K_Flip_Flop j_k_ff_1 (.J(and_4_out), .clk(CLK), .K(and_5_out), .Q(output_E));  // open: Qn, preset, en, reset
  and and_6 (AC_0__ac_i_1, CIL, d_ff_1_q);
  and and_7 (AC_3__ac_i_1, CIR, d_ff_1_q);
  and and_8 (AC_0__cin, ADD, d_ff_1_q);
endmodule
